# Fritzing sketch Schematic_Board_Layout (saved by Fritzing 0.9.3b)
circuit board: 6.88566cm x 5.36311cm
breadboards: 1

parts:
  U1 = IC, DIP package, 8 pins [chip_label=ILC7662 part_number=ICL7662CPA+-ND]
  U2 = IC, DIP package, 8 pins [chip_label=AMP03 part_number=AMP03GPZ-ND]
  U3 = IC, DIP package, 8 pins [chip_label=AMP03 part_number=AMP03GPZ-ND]
  R1 = Resistor [tolerance=±1% resistance=9.1k power=0.125W part_number=RN55D9101FB14 package=THT]
  R2 = Resistor [tolerance=±1% resistance=10k power=125mW part_number=RN55D1002FB14 package=THT]
  R3 = Resistor [tolerance=±5% resistance=200 power=500mW part_number=OF201JE package=THT]
  D1 = Schottky Diode [part_number=1N5817 package="300 mil [THT]"]
  UNO = Arduino Uno (Rev3) - ICSP [part_number=1050-1035-ND]
  J1 = male pin header, 10 pins [form="♂ (male)" part_number=609-3285-ND]
  S1 = SPST Switch [part_number=TS02CBE package=switch-spdt_kit]
  C9 = Film/Foil Capacitor [capacitance=100nF voltage=35V part_number=3006PH-ND package="5mm [THT, pp]"]
  C10 = Film/Foil Capacitor [capacitance=100nF voltage=35V part_number=3006PH-ND package="5mm [THT, pp]"]
  C8 = Ceramic Capacitor [capacitance=0.1µF voltage=35V part_number=TAP104K035SRW package="100 mil [THT, multilayer]"]
  C7 = Ceramic Capacitor [capacitance=0.1µF voltage=35V part_number=TAP104K035SRW package="100 mil [THT, multilayer]"]
  C3 = Ceramic Capacitor [capacitance=0.1µF voltage=35V part_number=TAP104K035SRW package="100 mil [THT, multilayer]"]
  C4 = Ceramic Capacitor [capacitance=0.1µF voltage=35V part_number=TAP104K035SRW package="100 mil [THT, multilayer]"]
  C5 = Ceramic Capacitor [capacitance=0.1µF voltage=35V part_number=TAP104K035SRW package="100 mil [THT, multilayer]"]
  C6 = Ceramic Capacitor [capacitance=0.1µF voltage=35V part_number=TAP104K035SRW package="100 mil [THT, multilayer]"]
  C2 = Electrolytic Capacitor [capacitance=10µF voltage=20V part_number=USR1E100MDD1TP package="100 mil [THT, electrolytic]"]
  C1 = Electrolytic Capacitor [capacitance=10µF voltage=20V part_number=USR1E100MDD1TP package="100 mil [THT, electrolytic]"]
  LED = LED - 5mm [color="Red (633nm)" part_number=B4301H1/5 package="5 mm [THT]"]
  U5 = LT1460 Micropower Precision Series Voltage Reference [part_number=LT1460GCZ-5#PBF-ND]
  U4 = LT1460 Micropower Precision Series Voltage Reference [part_number=LT1460GIZ-2.5#PDF-ND]

nets:
  N1: U1.pin2, C1.+
  GND/_GND_: U1.pin3, U1.pin6, U2.pin2, U3.pin2, R2.Pin_1, UNO.GND, J1.pin8, J1.pin9, S1.P, S1.S, C9.-, C10.-, C8.0, C7.0, C3.0, C4.0, C5.0, C6.0, C2.+, U5.GND, U4.GND
  N2: U1.pin4, C1.-
  N3: U1.pin5, U2.pin4, U3.pin4, C3.1, C5.1, C2.-
  9V/_VIN_: U1.pin8, U2.pin7, U3.pin7, R1.Pin_0, UNO.VIN, C8.1, C7.1, C4.1, C6.1, U5.Vin, U4.Vin
  N4: U2.pin1, U3.pin1, U4.Vout
  N5: U2.pin3, J1.pin3, C9.+
  _A0_: U2.pin5, U2.pin6, UNO.A0
  N6: U3.pin3, J1.pin5, C10.+
  _A1_: U3.pin5, U3.pin6, UNO.A1
  _A2_: R1.Pin_1, R2.Pin_0, D1.anode, UNO.A2
  _D11_: R3.Pin_0, UNO.ICSP_MOSI, UNO.D11_PWM/MOSI
  N7: R3.Pin_1, LED.cathode
  5V/_5V_: D1.cathode, UNO.5V
  _D9_: UNO.D9_PWM, S1.O
  _D10_: UNO.D10_PWM/SS, LED.anode
  _D12_: UNO.D12/MISO, J1.pin7
  _AREF_: UNO.AREF, U5.Vout

notes:
  RELAY N.O.
  X-Y Plotter to HP-GL Translator, Schematic, Proto Shield Rev 3, Arduino UNO, H
  Voltage converter ±9V
  X voltage level shifter
  Y voltage level shifter
  Voltage reference - 5.00V
  Voltage reference - 2.50V
  0.068µF
  X
  SHIELD GND
  Y
  RELAY COMM
  SIG GND
  BI-COLOR
  Tektronix 2232 X-Y Plotter
  Signal Conditioning Board
  Rev. H
  1 2 3 4 5 6 7 8 9 10
  RELAY
  N.O.
  COMM
  SIG
  GND
  -9V
  2.50V
  LED is 2-wire bi-color Red/Green
  This is the 'Arduino UNO (Rev 3) - ICSP' which includes both the ICSP 1 & 2 throughholes. I needed to manually reroute some traces. Instead, use the 'Arduino UNO (Rev 3)' part (no ICSP holes).

custom parts:
  LT1460 Micropower Precision Series Voltage Reference: The LT®1460 is a micropower bandgap reference that combines very high accuracy and low drift with low power dissipation and small package size. This series reference uses curvature compensation to obtain low temperature coefficient and trimmed precision thin-film resistors to achieve high output accuracy. The reference will supply up to 20mA with excellent line regulation characteristics,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

// code stored in the sketch: myTest.ino
/*
 ****************************************************************************************|
 * Tektronix 2232 Digital Storage Oscilloscope analog X-Y pen ploter to HP-GL 
 * translator. (Hewlett-Packard Graphics Language http://en.wikipedia.org/wiki/HPGL)
 * 
 * John Horstman
 * 3/2/2017 Rev G
 * 
 * This sketch continuously reads the X and Y analog pen plotter voltages, and the 
 * pen up/down signal, and packages the ADC values in successive HP-GL commands. The 
 * commands can be serially output to a file, via TeraTerm, or to a plotter application 
 * like PrintCapture at http://www.printcapture.com/.
 *  
 * The HP-GL commands used in this sketch are:
 * IN;  Initialize
 * PS:  Plot size
 * IP;  Input P1 & P2
 * SC;  Scale
 * SP;  Select pen
 * PU;  Pen UP
 * PD;  Pen DOWN
 * PA;  Plot Absolute
 * 
 * Example HPGL output of this sketch:
 * IN;
 * PS8900,8900;
 * IP0,0,8900,8900;
 * SC0,250,0,1023,1;
 * PU;
 * SP1;
 * PA77,984;
 * ...          // data points every 1.6 milliseconds
 * PD;
 * PA53,92;
 * ...
 * PU;
 * SP;
 * IN;
 * 
 * This sketch is for Arduino UNO with Proto Shield. The Proto Shield contains signal 
 * conditioning circuitry comprised of;
 * 1. Two (2) precision, unity-gain differential amplifiers (wired as summing amps) 
 *    to translate the ±2.5V analog X and Y voltages into 0 to 5V for the Arduino analog 
 *    pins.
 * 2. A 'charge pump' voltage converter to convert 9VDC to ±9VDC to power the amplifiers.
 * 3. A precision 2.50V voltage reference to the amplifiers for the voltage translation.
 * 4. A precision 5.00V voltage reference to the Arduino AREF pin.
 * 5. A voltage divider network so the 9V Vin can be reduced to 5V for the Arduino
 *    analog pin. A schottky diode protects the pin if a higher voltage power supply
 *    is used.
 * 6. A bi-color red/green LED as a Go/No Go indicator that the 9V power supply
 *    is connected, or not. This sketch will stay in the setup() routine until a 
 *    9VDC, or greater, power supply is plugged in to the Arduino. These IC's 
 *    cannot run accurately on the USB ~5V power!
 * 7. A slide switch to start the data stream and stop it when the plot is completed.
 * 8. A pair of capacitors to filter the DAC dithering of the plotter X-Y voltage signals.
 * 9. A 9-pin cable with DB-9 male connector for connection to the oscilloscope plotter 
 *    port.
 * 
 * Operation:
 * Slide switch to OFF.
 * Connect Arduino via DB-9 connector to oscilloscope plotter port. 
 * Connect Arduino USB to PC. Arduino powers up, LED is red.
 * Connect 9VDC power to Arduino. LED is green.
 * Launch listening application, like TeraTerm or PrintCapture. Ensure your application 
 *  is set to the Arduino COM port 6, 115200, 8, none, 1.
 * Slide switch to ON. (data stream commences)
 * Immediately press PLOT key on scope.
 * When scope plot completes immediately slide switch to OFF. (data stream halts)
 * Reset Arduino in order to start the next plot.
 ****************************************************************************************|
*/
//#define __serial_plotter // uncomment to calibrate with Arduino Serial Plotter tool
//#define __dummy_data // uncomment to use dummy data for testing

// The pins
#define TestPin 8      // Digital pin 8
#define SwitchPin 9    // Digital pin 9
#define LEDGreenPin 10 // Digital pin 10
#define LEDRedPin 11   // Digital pin 11
#define PenInputPin 12 // Digital pin 12
#define IdleLED 13     // Digital pin 13
#define X_voltage 0    // Analog pin A0
#define Y_voltage 1    // Analog pin A1
#define VinVoltage 2   // Analog pin A2
// The numbers
unsigned long LoopTime; // Marker for loop() delay timer
unsigned int PenState = HIGH;        // Default pen up
unsigned int OldPenState = PenState; //
const unsigned int numReadings = 8;       // Must be a power of two so we can right shift later
unsigned int Xreadings[numReadings];      // Arrays for computing moving average for smoothing
unsigned int Yreadings[numReadings];      //
unsigned int Xtotal = numReadings * 511;  // Arrays will be preloaded
unsigned int Ytotal = Xtotal;             //
unsigned int readIndex = 0;               //
const unsigned int dcXOffset = 21;  // Compensate for any DC offset. Adjust this to get approximately 511,511.
const unsigned int dcYOffset = 23;  //
// The strings
String ADCXStr; // ADC X counts string
String ADCYStr; // ADC Y counts string
String CmdStr;  // HPGL command string

#ifdef __dummy_data
const float slew = 614.0; // max slew rate is 3.0 volts/second = 614 counts/second (@5 volts = 1023 counts)
const float Freq = (1.0/PI) * (slew / 1023.0);  // This frequency sinusoidal will have that slew rate (at the zero crossing)
const float TWO_PI_F = 2.0 * PI * Freq;
#endif

/*
 * The Setup ****************************************************************************|
 */ 
void setup() {
  // Set I/O pins
  pinMode(TestPin, OUTPUT); // timing test pin
  pinMode(IdleLED, OUTPUT);
  pinMode(LEDRedPin, OUTPUT);
  pinMode(LEDGreenPin, OUTPUT);
  pinMode(SwitchPin, INPUT_PULLUP);
  pinMode(PenInputPin, INPUT_PULLUP); // Pen signal is from Normally Open (N.O.) relay contacts
  
  analogReference(DEFAULT);

  // Set LEDs
  digitalWrite(IdleLED, HIGH); // Turn on 'idle' LED
  digitalWrite(LEDRedPin, LOW); // Turn red/green LED off
  digitalWrite(LEDGreenPin, LOW);
  
  // initialize serial communication:
  Serial.begin(115200);

  // Check for 9V Vin external power, stay in setup() until 9V supply connected
  /*
   * Why 900 counts? To gaurantee that a 7.5±5%VDC power pack will not trigger the 
   * 'Go' signal under maximal conditions:
   * 7.5v+5%; R1Ω-1%; R2Ω+1%; USB 5v-5% (AREF); +3 counts (2 LSB ADC error)
   */
  while (analogRead(VinVoltage) < 900) {
    digitalWrite(LEDRedPin, HIGH); // Turn LED red (no-go)
    digitalWrite(LEDGreenPin, LOW);
    delay(100);
  } // Wait here until user plugs in a 9VDC, or greater, power supply
   
  // Vin OK, continue
  digitalWrite(LEDRedPin, LOW); // Turn LED green (go)
  digitalWrite(LEDGreenPin, HIGH);

  //Wait here for switch to be switched on (ground the pin)
  while (digitalRead(SwitchPin) == HIGH) {
    delay(100);
  } 
  // User is ready for data stream, let 'er rip!

  analogReference(EXTERNAL); // External precision 5.00V reference

  // Preset the averaging arrays
  for (int thisReading = 0; thisReading < numReadings; thisReading++) {
  Xreadings[thisReading] = 511;
  Yreadings[thisReading] = 511;
  }
  
  digitalWrite(IdleLED, LOW); // turn off 'idle' LED, transmission will commence (TX LED will light)

  // HP-GL plot header commands
  Serial.println("IN;"); // Initialize
  Serial.println("PS8900,8900;"); // Plot size; A-size
  Serial.println("IP0,0,8900,8900;"); // Input Scaling Points P1 & P2; A-size drawing (8.5" x 11", less margins)
  Serial.println("SC0,1023,0,1023,1;"); // Scale; Isotropic
  //Serial.println("OH;"); // Output hard clip limits
  //Serial.println("OP;"); // Output P1 & P2
  Serial.println("PU;"); // Pun Up
  Serial.println("SP1;"); // Select Pen 1
} // end setup

/*
 * The Loop *****************************************************************************|
*/
void loop() {
  LoopTime = micros(); // mark loop start
  
  // Read X, Y and Pen signals as close together as possible and compute a moving average for smoothing
  Xtotal -= Xreadings[readIndex]; // Subtract an old value from the total
  Ytotal -= Yreadings[readIndex]; //
  
  PenState = digitalRead(PenInputPin); // Read pen input; returns HIGH or LOW
  Xreadings[readIndex] = analogRead(X_voltage) - dcXOffset; // compensate for dc offset
  delayMicroseconds(8); // Delay one ADC clock cycle
  Yreadings[readIndex] = analogRead(Y_voltage) - dcYOffset;
  
  Xtotal += Xreadings[readIndex];   // Add the new value to the total
  Ytotal += Yreadings[readIndex++]; // Increment readIndex here
  readIndex %= numReadings;  // Wrap around readIndex here
  
  ADCXStr = Xtotal >> 3; // Total divided by numReadings (and convert to string)
  ADCYStr = Ytotal >> 3;
  //

  // If pen has changed state then output pen command
  // Pen UP signal is HIGH (relay open, interanl pull up resistor), pen DOWN is LOW (relay closed to ground)
  if (PenState != OldPenState) {
    (PenState == HIGH) ? (CmdStr = "PU;") : (CmdStr = "PD;");
    OldPenState = PenState; // Remember pen state
    Serial.println(CmdStr);
  }
  
  #ifdef __dummy_data
   // dummy data for now, plot a circle 
    float t = (float)millis() / 1000.0;
    float arg = TWO_PI_F * t;
    ADCXStr = int(511.5*cos(arg)+511.5);
    ADCYStr = int(511.5*sin(arg)+511.5);
  #endif

  #ifdef __serial_plotter
    int Pen;
    (PenState == HIGH) ? Pen = 10 : Pen = 0;  // View the Pen up/down signal
    CmdStr = "1023 0 " + ADCXStr + " " + ADCYStr + " " + Pen; // 1023 0 prevents autoscaling 
  #else
    // 'Plot Absolute' Ex: PA1023,250;
    CmdStr = "PA" + ADCXStr + "," + ADCYStr + ";";
  #endif
  
  Serial.println(CmdStr);

  // If switch went HIGH, output final commands, stop data stream, the plot is completed, wait here until RESET
  if (digitalRead(SwitchPin) == HIGH) {
    Serial.println("PU;");
    Serial.println("SP;");
    Serial.println("IN;");
    
    digitalWrite(IdleLED, HIGH); // turn on 'idle' LED
    
    while (true) {  // wait here for RESET
      delay(100);
    }
  }
  /* Wait here for remainder of loop time.
   * Full scale plot swing is 1023 counts in 1.667 seconds (5 volt full swing / 3.0 volts/second).
   * So, no more than one plot command every 1.630ms is necessary (1.667/1023). ~614 samples/second.
   */
  while (micros() - LoopTime < 1630) {;} // wait here for remainder of loop time 

  // Short (0.250µs) output pulse to test loop timing.
  PORTB |= B1; PORTB ^= B1; // digitalWrite(TestPin, HIGH); digitalWrite(TestPin, LOW);
}  // end loop

// code stored in the sketch: Tek_HPGL.ino
/*
 ****************************************************************************************|
 * Tektronix 2232 Digital Storage Oscilloscope analog X-Y pen ploter to HP-GL 
 * translator. (Hewlett-Packard Graphics Language http://en.wikipedia.org/wiki/HPGL)
 * 
 * John Horstman
 * 3/19/2017 Rev H
 * 
 * This sketch continuously reads the X and Y analog pen plotter voltages, and the 
 * pen up/down signal, and packages the ADC values in successive HP-GL commands. The 
 * commands can be serially output to a file, via TeraTerm, or to a plotter application 
 * like PrintCapture at http://www.printcapture.com/.
 *  
 * The HP-GL commands used in this sketch are:
 * IN;  Initialize
 * PS:  Plot size
 * IP;  Input P1 & P2
 * SC;  Scale
 * SP;  Select pen
 * PU;  Pen UP
 * PD;  Pen DOWN
 * PA;  Plot Absolute
 * 
 * Example HPGL output of this sketch:
 * IN;
 * PS8900,8900;
 * IP0,0,8900,8900;
 * SC0,250,0,1023,1;
 * PU;
 * SP1;
 * PA77,984;
 * ...          // data points every 1.6 milliseconds
 * PD;
 * PA53,92;
 * ...
 * PU;
 * SP;
 * IN;
 * 
 * This sketch is for Arduino UNO with Proto Shield. The Proto Shield contains signal 
 * conditioning circuitry comprised of;
 * 1. Two (2) precision, unity-gain differential amplifiers (wired as summing amps) 
 *    to translate the ±2.5V analog X and Y voltages into 0 to 5V for the Arduino analog 
 *    pins.
 * 2. A 'charge pump' voltage converter to convert 9VDC to ±9VDC to power the amplifiers.
 * 3. A precision 2.50V voltage reference to the amplifiers for the voltage translation.
 * 4. A precision 5.00V voltage reference to the Arduino AREF pin.
 * 5. A voltage divider network so the 9V Vin can be reduced to 5V for the Arduino
 *    analog pin. A schottky diode protects the pin if a higher voltage power supply
 *    is used.
 * 6. A bi-color red/green LED as a Go/No Go indicator that the 9V power supply
 *    is connected, or not. This sketch will stay in the setup() routine until a 
 *    9VDC, or greater, power supply is plugged in to the Arduino. These IC's 
 *    cannot run accurately on the USB ~5V power!
 * 7. A slide switch to start the data stream and stop it when the plot is completed.
 * 8. A pair of capacitors to filter the DAC dithering of the plotter X-Y voltage signals.
 * 9. A 9-pin cable with DB-9 male connector for connection to the oscilloscope plotter 
 *    port.
 * 
 * Operation:
 * Slide switch to OFF.
 * Connect Arduino via DB-9 connector to oscilloscope plotter port. 
 * Connect Arduino USB to PC. Arduino powers up, LED is red.
 * Connect 9VDC power to Arduino. LED is green.
 * Launch listening application, like TeraTerm or PrintCapture. Ensure your application 
 *  is set to the Arduino COM port 6, 115200, 8, none, 1.
 * Slide switch to ON. (data stream commences)
 * Immediately press PLOT key on scope.
 * When scope plot completes immediately slide switch to OFF. (data stream halts)
 * Reset Arduino in order to start the next plot.
 ****************************************************************************************|
*/
//#define __serial_plotter // uncomment to calibrate with Arduino Serial Plotter tool
//#define __dummy_data // uncomment to use dummy data for testing

// The pins
#define TestPin 8      // Digital pin 8
#define SwitchPin 9    // Digital pin 9
#define LEDGreenPin 10 // Digital pin 10
#define LEDRedPin 11   // Digital pin 11
#define PenInputPin 12 // Digital pin 12
#define IdleLED 13     // Digital pin 13
#define X_voltage 0    // Analog pin A0
#define Y_voltage 1    // Analog pin A1
#define VinVoltage 2   // Analog pin A2
// The numbers
unsigned long LoopTime; // Marker for loop() delay timer
unsigned int PenState = HIGH;        // Default pen up
unsigned int OldPenState = PenState; //
const unsigned int numReadings = 8;       // Must be a power of two so we can right shift later
unsigned int Xreadings[numReadings];      // Arrays for computing moving average for smoothing
unsigned int Yreadings[numReadings];      //
unsigned int Xtotal = numReadings * 511;  // Arrays will be preloaded
unsigned int Ytotal = Xtotal;             //
unsigned int readIndex = 0;               //
const unsigned int dcXOffset = 0; //21;  // Compensate for any DC offset. Adjust this to get approximately 511,511.
const unsigned int dcYOffset = 0; //23;  //
// The strings
String ADCXStr; // ADC X counts string
String ADCYStr; // ADC Y counts string
String CmdStr;  // HPGL command string

#ifdef __dummy_data
const float slew = 614.0; // max slew rate is 3.0 volts/second = 614 counts/second (@5 volts = 1023 counts)
const float Freq = (1.0/PI) * (slew / 1023.0);  // This frequency sinusoidal will have that slew rate (at the zero crossing)
const float TWO_PI_F = 2.0 * PI * Freq;
#endif

/*
 * The Setup ****************************************************************************|
 */ 
void setup() {
  // Set I/O pins
  pinMode(TestPin, OUTPUT); // timing test pin
  pinMode(IdleLED, OUTPUT);
  pinMode(LEDRedPin, OUTPUT);
  pinMode(LEDGreenPin, OUTPUT);
  pinMode(SwitchPin, INPUT_PULLUP);
  pinMode(PenInputPin, INPUT_PULLUP); // Pen signal is from Normally Open (N.O.) relay contacts
  
  analogReference(DEFAULT);

  // Set LEDs
  digitalWrite(IdleLED, HIGH); // Turn on 'idle' LED
  digitalWrite(LEDRedPin, LOW); // Turn red/green LED off
  digitalWrite(LEDGreenPin, LOW);
  
  // initialize serial communication:
  Serial.begin(115200);

  // Check for 9V Vin external power, stay in setup() until 9V supply connected
  /*
   * Why 900 counts? To gaurantee that a 7.5±5%VDC power pack will not trigger the 
   * 'Go' signal under maximal conditions:
   * 7.5v+5%; R1Ω-1%; R2Ω+1%; USB 5v-5% (AREF); +3 counts (2 LSB ADC error)
   */
  while (analogRead(VinVoltage) < 900) {
    digitalWrite(LEDRedPin, HIGH); // Turn LED red (no-go)
    digitalWrite(LEDGreenPin, LOW);
    delay(100);
  } // Wait here until user plugs in a 9VDC, or greater, power supply
   
  // Vin OK, continue
  digitalWrite(LEDRedPin, LOW); // Turn LED green (go)
  digitalWrite(LEDGreenPin, HIGH);

  //Wait here for switch to be switched on (ground the pin)
  while (digitalRead(SwitchPin) == HIGH) {
    delay(100);
  } 
  // User is ready for data stream, let 'er rip!

  analogReference(EXTERNAL); // External precision 5.00V reference

  // Preset the averaging arrays
  for (int thisReading = 0; thisReading < numReadings; thisReading++) {
  Xreadings[thisReading] = 511;
  Yreadings[thisReading] = 511;
  }
  
  digitalWrite(IdleLED, LOW); // turn off 'idle' LED, transmission will commence (TX LED will light)

  // HP-GL plot header commands
  Serial.println("IN;"); // Initialize
  Serial.println("PS8900,8900;"); // Plot size; A-size
  Serial.println("IP0,0,8900,8900;"); // Input Scaling Points P1 & P2; A-size drawing (8.5" x 11", less margins)
  Serial.println("SC0,1023,0,1023,1;"); // Scale; Isotropic
  //Serial.println("OH;"); // Output hard clip limits
  //Serial.println("OP;"); // Output P1 & P2
  Serial.println("PU;"); // Pun Up
  Serial.println("SP1;"); // Select Pen 1
} // end setup

/*
 * The Loop *****************************************************************************|
*/
void loop() {
  LoopTime = micros(); // mark loop start
  
  // Read X, Y and Pen signals as close together as possible and compute a moving average for smoothing
  Xtotal -= Xreadings[readIndex]; // Subtract an old value from the total
  Ytotal -= Yreadings[readIndex]; //
  
  PenState = digitalRead(PenInputPin); // Read pen input; returns HIGH or LOW
  Xreadings[readIndex] = analogRead(X_voltage) - dcXOffset; // compensate for dc offset
  delayMicroseconds(16); // Delay two ADC clock cycles (there is less 'jitter' on the Y readings than for a one ADC clock cycle dalay, don't ask me why)
  Yreadings[readIndex] = analogRead(Y_voltage) - dcYOffset;
  
  Xtotal += Xreadings[readIndex];   // Add the new value to the total
  Ytotal += Yreadings[readIndex++]; // Increment readIndex here
  readIndex %= numReadings;  // Wrap around readIndex here
  
  ADCXStr = Xtotal >> 3; // Total divided by numReadings (and convert to string)
  ADCYStr = Ytotal >> 3;
  //

  // If pen has changed state then output pen command
  // Pen UP signal is HIGH (relay open, interanl pull up resistor), pen DOWN is LOW (relay closed to ground)
  if (PenState != OldPenState) {
    (PenState == HIGH) ? (CmdStr = "PU;") : (CmdStr = "PD;");
    OldPenState = PenState; // Remember pen state
    Serial.println(CmdStr);
  }
  
  #ifdef __dummy_data
   // dummy data for now, plot a circle 
    float t = (float)millis() / 1000.0;
    float arg = TWO_PI_F * t;
    ADCXStr = int(511.5*cos(arg)+511.5);
    ADCYStr = int(511.5*sin(arg)+511.5);
  #endif

  #ifdef __serial_plotter
    int Pen;
    (PenState == HIGH) ? Pen = 10 : Pen = 0;  // View the Pen up/down signal
    CmdStr = "1023 0 " + ADCXStr + " " + ADCYStr + " " + Pen; // 1023 0 prevents autoscaling 
  #else
    // 'Plot Absolute' Ex: PA1023,250;
    CmdStr = "PA" + ADCXStr + "," + ADCYStr + ";";
  #endif
  
  Serial.println(CmdStr);

  // If switch went HIGH, output final commands, stop data stream, the plot is completed, wait here until RESET
  if (digitalRead(SwitchPin) == HIGH) {
    Serial.println("PU;");
    Serial.println("SP;");
    Serial.println("IN;");
    
    
    while (true) {  // wait here for RESET
      // flash 'idle' LED to indicate need for reset
      digitalWrite(IdleLED, HIGH);
      delay(200);
      digitalWrite(IdleLED, LOW);
      delay(300);
    }
  }
  /* Wait here for remainder of loop time.
   * Full scale plot swing is 1023 counts in 1.667 seconds (5 volt full swing / 3.0 volts/second).
   * So, no more than one plot command every 1.630ms is necessary (1.667/1023). ~614 samples/second.
   */
  while (micros() - LoopTime < 1630) {;} // wait here for remainder of loop time 

  // Short (0.250µs) output pulse to test loop timing.
  PORTB |= B1; PORTB ^= B1; // digitalWrite(TestPin, HIGH); digitalWrite(TestPin, LOW);
}  // end loop

// code stored in the sketch: Untitled.ino

/*
 ****************************************************************************************|
 * Tektronix 2232 Digital Storage Oscilloscope analog X-Y pen ploter to HP-GL 
 * translator. (Hewlett-Packard Graphics Language http://en.wikipedia.org/wiki/HPGL)
 * 
 * John Horstman
 * 1/26/2017 Rev A
 * 
 * This sketch continuously reads the X and Y analog pen plotter voltages, and the 
 * pen up/down signal, and packages the values in successive HP-GL commands. The commands
 * can be serially output to a file, via TeraTerm, or to a plotter application (like 
 * PrintCapture at http://www.printcapture.com/.
 *  
 * The HP-GL commands used in this sketch are:
 * IN;  Initialize
 * PU;  Pen UP
 * PD;  Pen DOWN
 * PAxxxx,xxxx; Plot Absolute, where xxxx is 0 through 1023
 * 
 * This sketch is for Arduino UNO with Proto Shield. The Proto Shield contains circuitry 
 * that has;
 * 1. A 'charge pump' voltage converter to convert 9VDC to ±9VDC for the amplifiers.
 * 2. Two (2) precision, unity-gain differential amplifiers (wired as summing amps) 
 *    to translate the ±2.5V analog X and Y voltages into 0 to 5V for the Arduino analog 
 *    pins.
 * 3. A precision 2.50V voltage reference for the amplifiers so the input voltage can be 
 *    translated.
 * 4. A precision 5.00V voltage reference for the Arduino AREF pin.
 * 5. A voltage divider resistor network so the 9V Vin can be reduced to 5V for the 
 *    Arduino analog pin. A zener diode protects the pin if a higher voltage power 
 *    supply is used.
 * 6. A bi-color red/green LED (with resistor) as a Go/No Go indicator that the 9V 
 *    power supply is connected, or not. This sketch will stay in the setup() routine 
 *    until a 9VDC, or greater, power supply is plugged in to the Arduino. These IC's 
 *    cannot run accurately on the USB ~5V power!
 * 7. A slide switch to start and stop the data stream when the plot is completed.
 * 8. A 9-pin cable with DB-9 male connector for connection to the oscilloscope plotter 
 *    port.
 * 
 * Operation:
 * Connect oscilloscope plotter port to Arduino via DB-9 connector. Arduino USB to PC.
 * Launch listening application, like TeraTerm or PrintCapture.
 * Reset Arduino.
 * Ensure your application connects to the Arduino through the USB port.
 * Slide switch to ON. (data stream commences)
 * Immediately press PLOT key on scope.
 * When scope plot completes immediately slide switch to OFF. (data stream halts)
 * Reset Arduino to beofre starting the next plot.
 ****************************************************************************************|
*/
  
String CmdStr;
String ADCXStr;
String ADCYStr;
unsigned int PenState;
unsigned int OldPenState = HIGH; // Pun UP
const unsigned int PenInputPin = 12;
const unsigned int LEDRedPin = 11;
const unsigned int LEDGreenPin = 10;
const unsigned int SwitchPin = 9;
bool enteredOnce = false;
/*
 * Analog pin A0: analog X voltage
 * Analog pin A1: analog Y voltage
 * Analog pin A2: Vin voltage
 */

// the setup routine runs once when you press reset:
void setup() {
  // initialize serial communication at 9600 bits per second:
  Serial.begin(9600);
  while (!Serial) {
    delay(100);
    }

  // Check for 9V Vin external power and wait here until Vin>8.55V
  analogReference(INTERNAL);
  delay(100);

  pinMode(LEDRedPin, OUTPUT);
  pinMode(LEDGreenPin, OUTPUT);
 
  digitalWrite(LEDRedPin, HIGH); // Turn LED red
  digitalWrite(LEDGreenPin, LOW);
   
  while (analogRead(A2) < 923) { // 8.55V - 2 LSB (ADC error)
  delay(100);
  } // Wait here until user plugs in a 9V, or greater, power supply
   
  digitalWrite(LEDRedPin, LOW); // Turn LED green
  digitalWrite(LEDGreenPin, HIGH);
  // Vin OK, continue

  //Wait here for switch to be switched (ground the pin)
  pinMode(SwitchPin, INPUT_PULLUP);
  delay(100);
  while (digitalRead(SwitchPin) == HIGH) {
    delay(100);
  } 
  // User is ready for data stream, let 'er rip!

  analogReference(EXTERNAL); // External precision 5.00V reference
  delay(100);
  
  pinMode(PenInputPin, INPUT_PULLUP); // Pen signal is from Normally Open (N.O.) relay contacts
  
  // First HP-GL command, Initialize
  Serial.println("IN;");
} // end setup

// the loop routine runs over and over again forever:
void loop() {
  PenState = digitalRead(PenInputPin); //Returns HIGH or LOW
  ADCXStr = analogRead(A0); // Read X voltage
  delay(1);
  ADCYStr = analogRead(A1); // Read Y voltage
  
  // If pen has changed state then output pen command
  // Pen UP signal is HIGH (relay open, interanl pull up resistor), pen DOWN is LOW (relay closed to ground)
  if (PenState != OldPenState) {
    (PenState == HIGH) ? (CmdStr = "PU;") : (CmdStr = "PD;");
    OldPenState = PenState;
    Serial.println(CmdStr);
  }
  
  // 'Plot Absolute' Ex: PA1023,1023;
  CmdStr = "PA" + ADCXStr + "," + ADCYStr + ";";
  
  Serial.println(CmdStr);

  //delay(?) // may need a delay here

  // If switch went HIGH, output last command, stop data stream, the plot is completed (wait here for switch to go LOW)
  while (digitalRead(SwitchPin) == HIGH) {
    if (enteredOnce == false) { // output the last command only once
      Serial.println("IN;");
      enteredOnce = true;
    }
    delay(100);
  }
  enteredOnce = false; // Switch went LOW, continue with loop() routine (but you really should hit reset after you finish your plot)
}
